# Fritzing sketch tankv5 (saved by Fritzing 0.9.3b)
breadboards: 1

parts:
  Raspberry_Pi_2 = Raspberry Pi 3 [part_number=RPI-3-V1.2]
  U4 = LIPO-2000mAh [package=lipo-2000]
  U5 = LIPO-1000mAh [package=lipo-1000]
  R5 = Resistor [tolerance=±5% resistance=1k package=THT]
  R6 = Resistor [tolerance=±5% resistance=1k package=THT]
  R7 = Resistor [tolerance=±5% resistance=1k package=THT]
  Part3 = Triple Axis Accelerometer Breakout - ADXL345
  MD03A2 = Dual VNH2SP30 Motor Driver [part_number=MD03A]
  hc-sr2 = hc-sr04
  J2 = Basic Servo
  M3 = DC Motor [part_number="Right Y = R"]
  M4 = DC Motor [part_number="LEFT, Y = R"]
  Part4 = PowerBoost 500 Charger
  U6 = USB Connectors [package=usb-microb]
  Part5 = FemtoBuck LED Driver
  Step_Down_Conv = FemtoBuck LED Driver
  Part7 = USB LiPoly Charger
  U7 = USB Connectors [package=usb-microb]

nets:
  3V3: Raspberry_Pi_2.3v3, Part3.VCC, Part3.CS
  N1: Raspberry_Pi_2.GPIO2, Part3.SDA
  N2: Raspberry_Pi_2.GPIO3, Part3.SCL
  N3: Raspberry_Pi_2.GIPO4, Part3.INT1, Part3.INT2
  GND: Raspberry_Pi_2.GND, R7.Pin_1, Part3.GND, hc-sr2.GND, J2.gnd, Step_Down_Conv.OUT-
  N4: Raspberry_Pi_2.GIPO17, MD03A2.1INa
  N5: Raspberry_Pi_2.GIPO22, MD03A2.1INb
  N6: Raspberry_Pi_2.GIPO21, hc-sr2.Trig
  N7: Raspberry_Pi_2.GIPO24, MD03A2.2INb#143
  N8: Raspberry_Pi_2.GIPO23, MD03A2.2INb#142
  N9: Raspberry_Pi_2.GIPO18, R5.Pin_0, R6.Pin_0
  N10: Raspberry_Pi_2.GIPO14, J2.pulse
  VIN: U4.+, MD03A2.VIN, Part5.OUT+, Step_Down_Conv.VIN, Part7.VBAT
  GND_2: U4.-, MD03A2.GND, Part5.OUT-, Step_Down_Conv.PGND, Part7.GND
  N11: U5.+, Part4.VBAT_IN
  N12: U5.-, Part4.GND_BAT_IN
  N13: R5.Pin_1, hc-sr2.Echo
  N14: R6.Pin_1, R7.Pin_0
  N15: MD03A2.OUT_1A, M4.pin_2
  N16: MD03A2.OUT_1B, M4.pin_1
  N17: MD03A2.OUT_2A, M3.pin_1
  N18: MD03A2.OUT_2B, M3.pin_2
  VCC: hc-sr2.VCC, J2.vcc, Step_Down_Conv.OUT+
  GND_3: Part4.GND, U6.GND
  N19: Part4.USB, U6.VBUS
  N20: Part5.PGND, U7.GND
  N21: Part5.VIN, U7.VBUS
